# Fritzing sketch weather station schematic (saved by Fritzing 0.9.3b)
circuit board: 5.10638cm x 4.01162cm

parts:
  part = ESP8266 WiFi Module [part_number=ESP8266]
  DHT11 = Humidity and Temperature Sensor RHT03
  OLED_128*64_I2C = Grove OLED 128x96

nets:
  N1: part.IO4, OLED_128*64_I2C.SDA
  VCC: part.3.3V, DHT11.Vcc, OLED_128*64_I2C.VCC
  GND: part.GND, DHT11.GND_1, OLED_128*64_I2C.GND
  N2: part.IO5, OLED_128*64_I2C.SCL
  N3: part.IO14, DHT11.Data-signal
